// Logisim project 718116_Somador.circ as structural Verilog: 4 circuits, main circuit main
module main (
  input  A0,
  input  B0,
  input  Ci0,
  output S0,
  output Co0,
  output S0_2,
  output Co0_2
);

  MeioSomador meiosomador_1 (.A(A0), .B(B0), .S(S0), .Co(Co0));
  SomadorCompleto somadorcompleto_1 (.A(A0), .B(B0), .Ci(Ci0), .S(S0_2), .Co(Co0_2));
endmodule

module MeioSomador (
  input  A,
  input  B,
  output S,
  output Co
);

  xor xor_1 (S, A, B);
  and and_1 (Co, A, B);
endmodule

module SomadorCompleto (
  input  A,
  input  B,
  input  Ci,
  output S,
  output Co
);

  wire meiosomador_1_co, meiosomador_1_s, meiosomador_2_co;

  MeioSomador meiosomador_1 (.A(A), .B(B), .S(meiosomador_1_s), .Co(meiosomador_1_co));
  MeioSomador meiosomador_2 (.A(meiosomador_1_s), .B(Ci), .S(S), .Co(meiosomador_2_co));
  or or_1 (Co, meiosomador_1_co, meiosomador_2_co);
endmodule

module Somador_4_bits (
  input  Ci0,
  input  A0,
  input  B0,
  input  A1,
  input  B1,
  input  A2,
  input  B2,
  input  A3,
  input  B3,
  output S0,
  output S1,
  output S2,
  output S3,
  output Flag
);

  wire somadorcompleto_1_p4, somadorcompleto_2_p4, somadorcompleto_3_p4;

  // SomadorCompleto somadorcompleto_1: pin names not known; wires that end beside it: A0, B0, Ci0, somadorcompleto_1_p4, S0
  // SomadorCompleto somadorcompleto_2: pin names not known; wires that end beside it: A1, B1, somadorcompleto_1_p4, somadorcompleto_2_p4, S1
  // SomadorCompleto somadorcompleto_3: pin names not known; wires that end beside it: A2, B2, somadorcompleto_2_p4, somadorcompleto_3_p4, S2
  // SomadorCompleto somadorcompleto_4: pin names not known; wires that end beside it: A3, B3, somadorcompleto_3_p4, Flag, S3
endmodule
