// Logisim project somador completo.circ as structural Verilog
module meio_somador (
  input  x0,
  input  y0,
  output s0,
  output co
);

  xor xor_1 (s0, x0, y0);
  and and_1 (co, x0, y0);
endmodule

module completo_somador (
  input  x1,
  input  y1,
  input  cin,
  output s1,
  output co
);

  wire meio_somador_1_co, meio_somador_1_s0, meio_somador_2_co;

  meio_somador meio_somador_1 (.x0(x1), .y0(y1), .s0(meio_somador_1_s0), .co(meio_somador_1_co));
  meio_somador meio_somador_2 (.x0(meio_somador_1_s0), .y0(cin), .s0(s1), .co(meio_somador_2_co));
  or or_1 (co, meio_somador_1_co, meio_somador_2_co);
endmodule

module _4_bit_sum (
  input  [3:0] x,
  input  [3:0] y,
  output [4:0] s
);

  wire completo_somador_1_co, completo_somador_2_co, completo_somador_3_co;

  completo_somador completo_somador_1 (.s1(s[0]), .x1(x[0]), .y1(y[0]), .cin(1'b0), .co(completo_somador_1_co));
  completo_somador completo_somador_2 (
    .s1(s[1]), .x1(x[1]), .y1(y[1]), .cin(completo_somador_1_co), .co(completo_somador_2_co));
  completo_somador completo_somador_3 (
    .s1(s[2]), .x1(x[2]), .y1(y[2]), .cin(completo_somador_2_co), .co(completo_somador_3_co));
  completo_somador completo_somador_4 (.s1(s[3]), .x1(x[3]), .y1(y[3]), .cin(completo_somador_3_co), .co(s[4]));
endmodule
