// Logisim project 4bitBinaryFullAdderWithFastCarry_SN54_74LS83A.circ as structural Verilog: 3 circuits, main circuit main
module main (
  input  A0,
  input  Ci,
  input  A1,
  input  A2,
  input  A3,
  input  B0,
  input  B1,
  input  B2,
  input  B3,
  output S1,
  output S2,
  output S2_2,
  output S4,
  output Co
);

  wire Decodificador_2_a, Decodificador_2_b, Decodificador_2_c, Decodificador_2_d, Decodificador_2_e,
       Decodificador_2_f, Decodificador_2_g, Decodificador_3_a, Decodificador_3_b, Decodificador_3_c,
       Decodificador_3_d, Decodificador_3_e, Decodificador_3_f, Decodificador_3_g, Decodificador_a,
       Decodificador_b, Decodificador_c, Decodificador_d, Decodificador_e, Decodificador_f, Decodificador_g;

  Decodificador Decodificador (
    .X3(A3), .X2(A2), .X1(A1), .A(Decodificador_a), .X0(A0), .B(Decodificador_b), .C(Decodificador_c),
    .D(Decodificador_d), .E(Decodificador_e), .F(Decodificador_f), .G(Decodificador_g));
  SN54_74LS83A Somador_4_bits (
    .C0(Ci), .A1(A0), .B1(B0), .A2(A1), .B2(B1), .A3(A2), .B3(B2), .A4(A3), .B4(B3), .S1(S1), .S2(S2),
    .S3(S2_2), .S4(S4), .C4(Co));
  Decodificador Decodificador_2 (
    .X3(B3), .X2(B2), .X1(B1), .A(Decodificador_2_a), .X0(B0), .B(Decodificador_2_b), .C(Decodificador_2_c),
    .D(Decodificador_2_d), .E(Decodificador_2_e), .F(Decodificador_2_f), .G(Decodificador_2_g));
  _7_Segment_Display u_7_segment_display_1 (
    .g(Decodificador_2_d), .f(Decodificador_2_c), .a(Decodificador_2_b), .b(Decodificador_2_a),
    .e(Decodificador_2_e), .d(Decodificador_2_f), .c(Decodificador_2_g));  // open: dp
  _7_Segment_Display u_7_segment_display_2 (
    .g(Decodificador_d), .f(Decodificador_c), .a(Decodificador_b), .b(Decodificador_a), .e(Decodificador_e),
    .d(Decodificador_f), .c(Decodificador_g));  // open: dp
  Decodificador Decodificador_3 (
    .X3(S4), .X2(S2_2), .X1(S2), .A(Decodificador_3_a), .X0(S1), .B(Decodificador_3_b),
    .C(Decodificador_3_c), .D(Decodificador_3_d), .E(Decodificador_3_e), .F(Decodificador_3_f),
    .G(Decodificador_3_g));
  _7_Segment_Display u_7_segment_display_3 (
    .g(Decodificador_3_d), .f(Decodificador_3_c), .a(Decodificador_3_b), .b(Decodificador_3_a),
    .e(Decodificador_3_e), .d(Decodificador_3_f), .c(Decodificador_3_g));  // open: dp
endmodule

module SN54_74LS83A (
  input  C0,
  input  A1,
  input  B1,
  input  A2,
  input  B2,
  input  A3,
  input  B3,
  input  A4,
  input  B4,
  output S1,
  output S2,
  output S3,
  output S4,
  output C4
);

  wire and_1_out, and_2_out, and_3_out, and_4_out, and_5_out, and_6_out, and_7_out, and_8_out, and_9_out,
       and_10_out, and_11_out, and_12_out, and_13_out, and_14_out, nand_1_out, nand_2_out, nand_3_out,
       nand_4_out, nor_1_out, nor_2_out, nor_3_out, nor_4_out, nor_5_out, nor_6_out, nor_7_out, not_1_out,
       not_2_out;

  not not_1 (not_1_out, C0);
  nor nor_1 (nor_1_out, A1, B1);
  not not_2 (not_2_out, not_1_out);
  and and_1 (and_1_out, ~nor_1_out, nand_1_out);  // AND_Gate
  xor xor_1 (S1, not_2_out, and_1_out);
  nand nand_1 (nand_1_out, A1, B1);
  and and_2 (and_2_out, not_1_out, nand_1_out);
  nand nand_2 (nand_2_out, A2, B2);
  nor nor_2 (nor_2_out, A2, B2);
  and and_3 (and_3_out, ~nor_2_out, nand_2_out);  // AND_Gate
  nor nor_3 (nor_3_out, and_2_out, nor_1_out);
  xor xor_2 (S2, nor_3_out, and_3_out);
  and and_4 (and_4_out, not_1_out, nand_1_out, nand_2_out);
  and and_5 (and_5_out, nand_2_out, nor_1_out);
  nor nor_4 (nor_4_out, and_4_out, and_5_out, nor_2_out);
  xor xor_3 (S3, nor_4_out, and_6_out);
  nor nor_5 (nor_5_out, A3, B3);
  nand nand_3 (nand_3_out, A3, B3);
  and and_6 (and_6_out, ~nor_5_out, nand_3_out);  // AND_Gate
  and and_7 (and_7_out, not_1_out, nand_1_out, nand_2_out, nand_3_out);
  and and_8 (and_8_out, nand_2_out, nand_3_out, nor_1_out);
  and and_9 (and_9_out, nand_3_out, nor_2_out);
  nor nor_6 (nor_6_out, and_7_out, and_8_out, and_9_out, nor_5_out);
  xor xor_4 (S4, nor_6_out, and_10_out);
  nor nor_7 (nor_7_out, A4, B4);
  and and_10 (and_10_out, ~nor_7_out, nand_4_out);  // AND_Gate
  nand nand_4 (nand_4_out, A4, B4);
  and and_11 (and_11_out, nand_2_out, nand_3_out, nand_4_out, nor_1_out);
  and and_12 (and_12_out, not_1_out, nand_1_out, nand_2_out, nand_3_out, nand_4_out);
  and and_13 (and_13_out, nand_3_out, nand_4_out, nor_2_out);
  nor nor_8 (C4, and_12_out, and_11_out, and_13_out, and_14_out, nor_7_out);
  and and_14 (and_14_out, nand_4_out, nor_5_out);
endmodule

module Decodificador (
  input  X3,
  input  X2,
  input  X1,
  input  X0,
  output A,
  output B,
  output C,
  output D,
  output E,
  output F,
  output G
);

  wire and_1_out, and_2_out, and_3_out, and_4_out, and_5_out, and_6_out, and_7_out, and_8_out, and_9_out,
       and_10_out, and_11_out, and_12_out, and_13_out, and_14_out, and_15_out, and_16_out, and_17_out,
       and_18_out, and_19_out, and_20_out, and_21_out, and_22_out, and_23_out, and_24_out, and_25_out,
       and_26_out, and_27_out, and_28_out, and_29_out, and_30_out, and_31_out, and_32_out, and_33_out,
       and_34_out, and_35_out, not_1_out, not_2_out, not_3_out, not_4_out, not_5_out, not_6_out, not_7_out,
       not_8_out, not_9_out, not_10_out, not_11_out, not_12_out, not_13_out, not_14_out, not_15_out,
       not_16_out, not_17_out, not_18_out, not_19_out, not_20_out, not_21_out, not_22_out, not_23_out,
       not_24_out, not_25_out, not_26_out, not_27_out, not_28_out, not_29_out, not_30_out, not_31_out,
       not_32_out, not_33_out, not_34_out, not_35_out, not_36_out, not_37_out, not_38_out, not_39_out,
       not_40_out, not_41_out, not_42_out, not_43_out;

  not not_1 (not_1_out, X3);
  and and_1 (and_1_out, not_1_out, not_2_out);
  not not_2 (not_2_out, X2);
  not not_3 (not_3_out, X3);
  not not_4 (not_4_out, X1);
  and and_2 (and_2_out, not_3_out, not_4_out, not_5_out);
  not not_5 (not_5_out, X0);
  not not_6 (not_6_out, X2);
  and and_3 (and_3_out, not_6_out, not_7_out);
  not not_7 (not_7_out, X0);
  not not_8 (not_8_out, X3);
  and and_4 (and_4_out, not_8_out, X1, X0);
  not not_9 (not_9_out, X1);
  and and_5 (and_5_out, X3, not_9_out, X0);
  not not_10 (not_10_out, X2);
  and and_6 (and_6_out, not_10_out, not_11_out);
  not not_11 (not_11_out, X0);
  not not_12 (not_12_out, X3);
  and and_7 (and_7_out, not_12_out, X1);
  not not_13 (not_13_out, X3);
  and and_8 (and_8_out, not_13_out, X2, X0);
  and and_9 (and_9_out, X2, X1);
  and and_10 (and_10_out, X3, not_14_out, not_15_out);
  not not_14 (not_14_out, X2);
  not not_15 (not_15_out, X1);
  and and_11 (and_11_out, X3, not_16_out);
  not not_16 (not_16_out, X0);
  not not_17 (not_17_out, X1);
  and and_12 (and_12_out, not_17_out, not_18_out);
  not not_18 (not_18_out, X0);
  not not_19 (not_19_out, X3);
  and and_13 (and_13_out, not_19_out, X2, not_20_out);
  not not_20 (not_20_out, X1);
  and and_14 (and_14_out, X2, not_21_out);
  not not_21 (not_21_out, X0);
  and and_15 (and_15_out, X3, not_22_out);
  not not_22 (not_22_out, X2);
  and and_16 (and_16_out, X3, X1);
  not not_23 (not_23_out, X2);
  and and_17 (and_17_out, not_23_out, X1);
  and and_18 (and_18_out, X1, not_24_out);
  not not_24 (not_24_out, X0);
  not not_25 (not_25_out, X3);
  and and_19 (and_19_out, not_25_out, X2, not_26_out);
  not not_26 (not_26_out, X1);
  and and_20 (and_20_out, X3, not_27_out);
  not not_27 (not_27_out, X2);
  and and_21 (and_21_out, X3, X0);
  not not_28 (not_28_out, X2);
  and and_22 (and_22_out, not_28_out, not_29_out);
  not not_29 (not_29_out, X0);
  and and_23 (and_23_out, X1, not_30_out);
  not not_30 (not_30_out, X0);
  and and_24 (and_24_out, X3, X1);
  and and_25 (and_25_out, X3, X2);
  not not_31 (not_31_out, X3);
  and and_26 (and_26_out, not_31_out, not_32_out, not_33_out);
  not not_32 (not_32_out, X2);
  not not_33 (not_33_out, X0);
  not not_34 (not_34_out, X2);
  and and_27 (and_27_out, not_34_out, X1, X0);
  not not_35 (not_35_out, X1);
  and and_28 (and_28_out, X2, not_35_out, X0);
  and and_29 (and_29_out, X2, X1, not_36_out);
  not not_36 (not_36_out, X0);
  and and_30 (and_30_out, X3, not_37_out);
  not not_37 (not_37_out, X1);
  not not_38 (not_38_out, X3);
  and and_31 (and_31_out, not_38_out, not_39_out);
  not not_39 (not_39_out, X1);
  not not_40 (not_40_out, X3);
  and and_32 (and_32_out, not_40_out, X0);
  not not_41 (not_41_out, X1);
  and and_33 (and_33_out, not_41_out, X0);
  not not_42 (not_42_out, X3);
  and and_34 (and_34_out, not_42_out, X2);
  and and_35 (and_35_out, X3, not_43_out);
  not not_43 (not_43_out, X2);
  or or_1 (A, and_1_out, and_2_out, and_3_out, and_4_out, and_5_out);
  or or_2 (C, and_12_out, and_13_out, and_14_out, and_15_out, and_16_out);
  or or_3 (D, and_17_out, and_18_out, and_19_out, and_20_out, and_21_out);
  or or_4 (E, and_22_out, and_23_out, and_24_out, and_25_out);
  or or_5 (F, and_26_out, and_27_out, and_28_out, and_29_out, and_30_out);
  or or_6 (G, and_31_out, and_32_out, and_33_out, and_34_out, and_35_out);
  or or_7 (B, and_6_out, and_7_out, and_8_out, and_9_out, and_10_out, and_11_out);
endmodule
