// Logisim project 4_x_4.circ as structural Verilog
module FA (
  input  Ci,
  input  Ai,
  input  Bi,
  output So,
  output Co
);

  wire and_1_out, and_2_out, and_3_out, xor_1_out;

  xor xor_1 (xor_1_out, Ci, Ai);
  and and_1 (and_1_out, Ai, Bi);
  and and_2 (and_2_out, Ai, Ci);
  and and_3 (and_3_out, Ci, Bi);
  xor xor_2 (So, xor_1_out, Bi);
  or or_1 (Co, and_1_out, and_2_out, and_3_out);
endmodule

module _4_x_4 (
  input  a3,
  input  a2,
  input  a1,
  input  a0,
  input  b3,
  input  b2,
  input  b1,
  input  b0,
  output out_9,
  output out_10,
  output out_11,
  output out_12,
  output out_13,
  output out_14,
  output out_15,
  output out_16
);

  wire and_1_out, and_2_out, and_3_out, and_4_out, and_5_out, and_6_out, and_7_out, and_8_out, and_9_out,
       and_10_out, and_11_out, and_12_out, and_13_out, and_14_out, and_15_out, fa_1_co, fa_1_so, fa_3_co,
       fa_3_so, fa_4_co, fa_4_so, fa_5_co, fa_6_co, fa_6_so, fa_7_co, fa_7_so, fa_8_co, fa_9_co, fa_10_co,
       fa_10_so, fa_11_co, fa_12_co;

  and and_1 (and_1_out, a3, b2);
  and and_2 (and_2_out, a2, b2);
  FA fa_1 (.Ci(fa_4_co), .Ai(fa_3_co), .Bi(and_1_out), .So(fa_1_so), .Co(fa_1_co));
  and and_3 (and_3_out, a3, b3);
  FA fa_2 (.Ci(fa_5_co), .Ai(fa_1_co), .Bi(and_3_out), .So(out_10), .Co(out_9));
  and and_4 (and_4_out, a3, b1);
  FA fa_3 (.Ci(fa_6_co), .Ai(1'b0), .Bi(and_4_out), .So(fa_3_so), .Co(fa_3_co));
  FA fa_4 (.Ci(fa_7_co), .Ai(fa_3_so), .Bi(and_2_out), .So(fa_4_so), .Co(fa_4_co));
  and and_5 (and_5_out, a2, b3);
  FA fa_5 (.Ci(fa_8_co), .Ai(fa_1_so), .Bi(and_5_out), .So(out_11), .Co(fa_5_co));
  and and_6 (and_6_out, a2, b1);
  FA fa_6 (.Ci(fa_10_co), .Ai(and_9_out), .Bi(and_6_out), .So(fa_6_so), .Co(fa_6_co));
  and and_7 (and_7_out, a1, b2);
  FA fa_7 (.Ci(fa_11_co), .Ai(fa_6_so), .Bi(and_7_out), .So(fa_7_so), .Co(fa_7_co));
  and and_8 (and_8_out, a1, b3);
  FA fa_8 (.Ci(fa_9_co), .Ai(fa_4_so), .Bi(and_8_out), .So(out_12), .Co(fa_8_co));
  and and_9 (and_9_out, a3, b0);
  and and_10 (and_10_out, a0, b3);
  FA fa_9 (.Ci(1'b0), .Ai(fa_7_so), .Bi(and_10_out), .So(out_13), .Co(fa_9_co));
  and and_11 (and_11_out, a2, b0);
  and and_12 (and_12_out, a1, b1);
  and and_13 (and_13_out, a0, b1);
  FA fa_10 (.Ci(fa_12_co), .Ai(and_11_out), .Bi(and_12_out), .So(fa_10_so), .Co(fa_10_co));
  and and_14 (and_14_out, a0, b2);
  FA fa_11 (.Ci(1'b0), .Ai(fa_10_so), .Bi(and_14_out), .So(out_14), .Co(fa_11_co));
  and and_15 (and_15_out, a1, b0);
  FA fa_12 (.Ci(1'b0), .Ai(and_15_out), .Bi(and_13_out), .So(out_15), .Co(fa_12_co));
  and and_16 (out_16, a0, b0);
endmodule
