// Logisim project ALU.circ as structural Verilog: 5 circuits, main circuit main
module main (
  input  Binvert,
  input  [1:0] Op,
  input  A,
  input  B,
  output Result,
  output Carry_Out
);

  ULA_1 ula_1_1 (
    .A(A), .B(B), .Result(Result), .Binvert(Binvert), .Carry_In(Binvert), .Operation(Op),
    .Carry_Out(Carry_Out));
endmodule

module ULA_1 (
  input  Binvert,
  input  Carry_In,
  input  [1:0] Operation,
  input  A,
  input  B,
  output Result,
  output Carry_Out
);

  wire and_1_out, MUX_1_result, not_1_out, not_2_out, or_1_out, Somador_Completo_s;

  not not_1 (not_1_out, B);
  MUX_1 MUX_1 (.X(B), .Y(not_1_out), .Result(MUX_1_result), .Op(Binvert));
  and and_1 (and_1_out, A, MUX_1_result);
  or or_1 (or_1_out, A, MUX_1_result);
  not not_2 (not_2_out, A);
  SomadorCompleto Somador_Completo (.A(A), .B(MUX_1_result), .Ci(Carry_In), .S(Somador_Completo_s), .Co(Carry_Out));
  MUX_4 MUX_4 (.A0(and_1_out), .A1(or_1_out), .A2(not_2_out), .A3(Somador_Completo_s), .Result(Result), .Op(Operation));
endmodule

module MUX_1 (
  input  Op,
  input  X,
  input  Y,
  output Result
);

  wire and_1_out, and_2_out, not_1_out;

  not not_1 (not_1_out, Op);
  and and_1 (and_1_out, X, not_1_out);
  and and_2 (and_2_out, Y, Op);
  or or_1 (Result, and_1_out, and_2_out);
endmodule

module MUX_4 (
  input  [1:0] Op,
  input  A0,
  input  A1,
  input  A2,
  input  A3,
  output Result
);

  wire and_1_out, and_2_out, and_3_out, and_4_out, not_1_out, not_2_out, not_3_out, not_4_out;

  not not_1 (not_1_out, Op[0]);
  not not_2 (not_2_out, Op[1]);
  not not_3 (not_3_out, Op[1]);
  not not_4 (not_4_out, Op[0]);
  and and_1 (and_1_out, A0, not_1_out, not_2_out);
  and and_2 (and_2_out, A1, Op[0], not_3_out);
  and and_3 (and_3_out, A2, not_4_out, Op[1]);
  and and_4 (and_4_out, A3, Op[0], Op[1]);
  or or_1 (Result, and_1_out, and_2_out, and_3_out, and_4_out);
endmodule

module ULA_4 (
  input  [3:0] A,
  input  [3:0] B,
  input  Binvert,
  input  [1:0] Op,
  output [3:0] out_5,
  output Carry_Out
);

  wire ULA_2_carry_out, ULA_3_carry_out, ULA_carry_out;

  ULA_1 ULA (
    .A(A[0]), .B(B[0]), .Result(out_5[0]), .Binvert(Binvert), .Carry_In(Binvert), .Operation(Op),
    .Carry_Out(ULA_carry_out));
  ULA_1 ULA_2 (
    .A(A[1]), .B(B[1]), .Result(out_5[1]), .Binvert(Binvert), .Carry_In(ULA_carry_out), .Operation(Op),
    .Carry_Out(ULA_2_carry_out));
  ULA_1 ULA_3 (
    .A(A[2]), .B(B[2]), .Result(out_5[2]), .Binvert(Binvert), .Carry_In(ULA_2_carry_out), .Operation(Op),
    .Carry_Out(ULA_3_carry_out));
  ULA_1 ULA_4 (
    .A(A[3]), .B(B[3]), .Result(out_5[3]), .Binvert(Binvert), .Carry_In(ULA_3_carry_out), .Operation(Op),
    .Carry_Out(Carry_Out));
endmodule
